// Logisim project ex1.circ as structural Verilog: 6 circuits, main circuit NOR1
module NAND1 (
  input  A,
  input  B,
  output RESULT
);

  wire and_1_out;

  not not_1 (RESULT, and_1_out);
  and and_1 (and_1_out, A, B);

  // Notes on the sheet:
  //   PUT CIRCUITRY HERE
endmodule

module NOR1 (
  input  A,
  input  B,
  output RESULT
);

  wire or_1_out;

  not not_1 (RESULT, or_1_out);
  or or_1 (or_1_out, A, B);

  // Notes on the sheet:
  //   PUT CIRCUITRY HERE
endmodule

module XOR1 (
  input  A,
  input  B,
  output RESULT
);

  wire and_1_out, nor1_1_result;

  and and_1 (and_1_out, A, B);
  NOR1 nor1_1 (.A(A), .B(B), .RESULT(nor1_1_result));
  NOR1 nor1_2 (.A(and_1_out), .B(nor1_1_result), .RESULT(RESULT));

  // Notes on the sheet:
  //   PUT CIRCUITRY HERE
endmodule

module MUX2 (
  input  A,
  input  B,
  input  Sel,
  output RESULT
);

  wire and_1_out, and_2_out, not_1_out;

  not not_1 (not_1_out, Sel);
  and and_1 (and_1_out, A, not_1_out);
  and and_2 (and_2_out, B, Sel);
  or or_1 (RESULT, and_1_out, and_2_out);

  // Notes on the sheet:
  //   PUT CIRCUITRY HERE
endmodule

module MUX4 (
  input  A,
  input  B,
  input  C,
  input  D,
  input  Sel1,
  input  Sel2,
  output RESULT
);

  wire and_1_out, and_2_out, and_3_out, and_4_out, and_5_out, and_6_out, and_7_out, and_8_out, not_1_out,
       not_2_out;

  not not_1 (not_1_out, Sel1);
  not not_2 (not_2_out, Sel2);
  and and_1 (and_1_out, A, and_2_out);
  and and_2 (and_2_out, not_1_out, not_2_out);
  and and_3 (and_3_out, B, and_4_out);
  and and_4 (and_4_out, Sel1, not_2_out);
  and and_5 (and_5_out, C, and_6_out);
  and and_6 (and_6_out, not_1_out, Sel2);
  and and_7 (and_7_out, D, and_8_out);
  and and_8 (and_8_out, Sel1, Sel2);
  or or_1 (RESULT, and_1_out, and_3_out, and_5_out, and_7_out);

  // Notes on the sheet:
  //   PUT CIRCUITRY HERE
endmodule

module Half_Adder (
  input  A,
  input  B,
  output SUM,
  output CARRY
);

  wire or_1_out;

  or or_1 (or_1_out, A, B);
  and and_1 (CARRY, A, B);
  XOR1 xor1_1 (.A(or_1_out), .B(CARRY), .RESULT(SUM));
endmodule
