// Logisim project ex2.circ as structural Verilog: 5 circuits, main circuit rotr
module rotr (
  input  [15:0] A,
  input  [3:0] B,
  output [15:0] Out1
);

  wire [15:0] and_1_out, and_2_out, and_3_out, and_4_out, and_5_out, and_6_out, and_7_out, and_8_out, done2,
       done4, done8, not_1_out, not_2_out, not_3_out, not_4_out, r1, r2, r4, r8, rot1_1_out_2, rot2_1_out_2,
       rot4_1_out_2, rot8_1_out_2;

  assign r1 = {{15{B[0]}}, B[0]};  // Bit_Extender bit_extender_1
  assign r2 = {{15{B[1]}}, B[1]};  // Bit_Extender bit_extender_2
  assign r4 = {{15{B[2]}}, B[2]};  // Bit_Extender bit_extender_3
  assign r8 = {{15{B[3]}}, B[3]};  // Bit_Extender bit_extender_4
  rot8 rot8_1 (.in_1(A), .out_2(rot8_1_out_2));
  assign not_1_out = ~r8;  // NOT_Gate not_1, 16 bits wide
  rot4 rot4_1 (.in_1(done8), .out_2(rot4_1_out_2));
  assign not_2_out = ~r4;  // NOT_Gate not_2, 16 bits wide
  assign and_1_out = r8 & rot8_1_out_2;  // AND_Gate and_1, 16 bits wide
  assign and_2_out = not_1_out & A;  // AND_Gate and_2, 16 bits wide
  assign and_3_out = r4 & rot4_1_out_2;  // AND_Gate and_3, 16 bits wide
  assign and_4_out = not_2_out & done8;  // AND_Gate and_4, 16 bits wide
  assign done8 = and_1_out | and_2_out;  // OR_Gate or_1, 16 bits wide
  assign done4 = and_3_out | and_4_out;  // OR_Gate or_2, 16 bits wide
  rot2 rot2_1 (.in_1(done4), .out_2(rot2_1_out_2));
  rot1 rot1_1 (.in_1(done2), .out_2(rot1_1_out_2));
  assign not_3_out = ~r2;  // NOT_Gate not_3, 16 bits wide
  assign not_4_out = ~r1;  // NOT_Gate not_4, 16 bits wide
  assign and_5_out = r2 & rot2_1_out_2;  // AND_Gate and_5, 16 bits wide
  assign done2 = and_5_out | and_6_out;  // OR_Gate or_3, 16 bits wide
  assign and_6_out = not_3_out & done4;  // AND_Gate and_6, 16 bits wide
  assign and_7_out = r1 & rot1_1_out_2;  // AND_Gate and_7, 16 bits wide
  assign Out1 = and_7_out | and_8_out;  // OR_Gate or_4, 16 bits wide
  assign and_8_out = not_4_out & done2;  // AND_Gate and_8, 16 bits wide

  // Other names for the same wires on the sheet: done[15:0] = Out1

  // Notes on the sheet:
  //   PUT CIRCUITRY HERE
endmodule

module rot8 (
  input  [15:0] in_1,
  output [15:0] out_2
);

  wire [15:0] rot4_1_out_2;

  rot4 rot4_1 (.in_1(in_1), .out_2(rot4_1_out_2));
  rot4 rot4_2 (.in_1(rot4_1_out_2), .out_2(out_2));

  // Notes on the sheet:
  //   PUT CIRCUITRY HERE
endmodule

module rot4 (
  input  [15:0] in_1,
  output [15:0] out_2
);

  wire [15:0] rot2_1_out_2;

  rot2 rot2_1 (.in_1(in_1), .out_2(rot2_1_out_2));
  rot2 rot2_2 (.in_1(rot2_1_out_2), .out_2(out_2));

  // Notes on the sheet:
  //   PUT CIRCUITRY HERE
endmodule

module rot2 (
  input  [15:0] in_1,
  output [15:0] out_2
);

  wire [15:0] rot1_1_out_2;

  rot1 rot1_1 (.in_1(in_1), .out_2(rot1_1_out_2));
  rot1 rot1_2 (.in_1(rot1_1_out_2), .out_2(out_2));

  // Notes on the sheet:
  //   PUT CIRCUITRY HERE
endmodule

module rot1 (
  input  [15:0] in_1,
  output [15:0] out_2
);


  assign out_2 = {in_1[0], in_1[15:1]};

  // Notes on the sheet:
  //   PUT CIRCUITRY HERE
endmodule
