// Logisim project alu.circ as structural Verilog: 18 circuits, main circuit alu
module alu (
  input  [31:0] A,
  input  [31:0] B,
  input  [3:0] ALUSel,
  output [31:0] Result
);

  wire [31:0] add_1_o, and2_1_o, cnto_1_o, div_1_o, divu_1_o, mulh_1_o, mulhu_1_o, mult_1_o, or2_1_o,
       remu_1_o, sll2_1_o, slt_1_o, sra2_1_o, srl2_1_o, sub_1_o, xor2_1_o;

  and2 and2_1 (.A(A), .B(B), .O(and2_1_o));
  or2 or2_1 (.A(A), .B(B), .O(or2_1_o));
  xor2 xor2_1 (.A(A), .B(B), .O(xor2_1_o));
  add add_1 (.A(A), .B(B), .O(add_1_o));
  sub sub_1 (.A(A), .B(B), .O(sub_1_o));
  mult mult_1 (.A(A), .B(B), .O(mult_1_o));
  mulhu mulhu_1 (.A(A), .B(B), .O(mulhu_1_o));
  mulh mulh_1 (.A(A), .B(B), .O(mulh_1_o));
  divu divu_1 (.A(A), .B(B), .O(divu_1_o));
  div div_1 (.A(A), .B(B), .O(div_1_o));
  remu remu_1 (.A(A), .B(B), .O(remu_1_o));
  srl2 srl2_1 (.A(A), .B(B), .O(srl2_1_o));
  sra2 sra2_1 (.A(A), .B(B), .O(sra2_1_o));
  slt slt_1 (.A(A), .B(B), .O(slt_1_o));
  sll2 sll2_1 (.A(A), .B(B), .O(sll2_1_o));
  cnto cnto_1 (.A(A), .B(B), .O(cnto_1_o));
  Multiplexer #(.select(4), .width(32), .enable("false")) multiplexer_1 (
    .in0(and2_1_o), .in1(or2_1_o), .in2(xor2_1_o), .in3(add_1_o), .in4(sub_1_o), .in5(mult_1_o),
    .in6(mulhu_1_o), .in7(mulh_1_o), .in8(divu_1_o), .in9(div_1_o), .in10(remu_1_o), .in11(srl2_1_o),
    .in12(sra2_1_o), .in13(slt_1_o), .in14(sll2_1_o), .in15(cnto_1_o), .out(Result), .sel(ALUSel));

  // Notes on the sheet:
  //   INPUTS to your circuit
  //   DON'T CHANGE THE LOCATIONS OF THE INPUTS AND OUTPUTS!
  //   OUTPUT from your circuit
endmodule

module and2 (
  input  [31:0] A,
  input  [31:0] B,
  output [31:0] O
);

  assign O = A & B;  // AND_Gate and_1, 32 bits wide
endmodule

module or2 (
  input  [31:0] A,
  input  [31:0] B,
  output [31:0] O
);

  assign O = A | B;  // OR_Gate or_1, 32 bits wide
endmodule

module xor2 (
  input  [31:0] A,
  input  [31:0] B,
  output [31:0] O
);

  assign O = A ^ B;  // XOR_Gate xor_1, 32 bits wide
endmodule

module add (
  input  [31:0] A,
  input  [31:0] B,
  output [31:0] O
);

  Adder #(.width(32)) adder_1 (.a(A), .b(B), .out(O));  // open: cin, cout
endmodule

module sub (
  input  [31:0] A,
  input  [31:0] B,
  output [31:0] O
);

  Subtractor #(.width(32)) subtractor_1 (.a(A), .b(B), .out(O));  // open: bin, bout
endmodule

module mult (
  input  [31:0] A,
  input  [31:0] B,
  output [31:0] O
);

  Multiplier #(.width(32)) multiplier_1 (.a(A), .b(B), .out(O));  // open: cin, cout
endmodule

module mulhu (
  input  [31:0] A,
  input  [31:0] B,
  output [31:0] O
);

  Multiplier #(.width(32)) multiplier_1 (.a(A), .b(B), .cout(O));  // open: out, cin
endmodule

module mulh (
  input  [31:0] A,
  input  [31:0] B,
  output [31:0] O
);

  wire abs2_1_sign, abs2_2_sign, adder_1_cout, xnor_1_out;
  wire [31:0] abs2_1_o, abs2_2_o, adder_2_out, bit_extender_1_out, multiplier_1_cout, multiplier_1_out,
       not_1_out, not_2_out;

  abs2 abs2_1 (.A(A), .O(abs2_1_o), .Sign(abs2_1_sign));
  abs2 abs2_2 (.A(B), .O(abs2_2_o), .Sign(abs2_2_sign));
  Multiplier #(.width(32)) multiplier_1 (
    .a(abs2_1_o), .b(abs2_2_o), .out(multiplier_1_out), .cout(multiplier_1_cout));  // open: cin
  assign not_1_out = ~multiplier_1_out;  // NOT_Gate not_1, 32 bits wide
  assign not_2_out = ~multiplier_1_cout;  // NOT_Gate not_2, 32 bits wide
  xnor xnor_1 (xnor_1_out, abs2_1_sign, abs2_2_sign);
  Adder #(.width(32)) adder_1 (.a(not_1_out), .b(32'h1), .cout(adder_1_cout));  // open: out, cin
  assign bit_extender_1_out = {{31{1'b0}}, adder_1_cout};  // Bit_Extender bit_extender_1
  Adder #(.width(32)) adder_2 (.a(bit_extender_1_out), .b(not_2_out), .out(adder_2_out));  // open: cin, cout
  Multiplexer #(.width(32), .enable("false")) multiplexer_1 (
    .in0(adder_2_out), .in1(multiplier_1_cout), .out(O), .sel(xnor_1_out));
endmodule

module divu (
  input  [31:0] A,
  input  [31:0] B,
  output [31:0] O
);

  Divider #(.width(32)) divider_1 (.a(A), .b(B), .out(O));  // open: upper, rem
endmodule

module div (
  input  [31:0] A,
  input  [31:0] B,
  output [31:0] O
);

  wire abs2_1_sign, abs2_2_sign, xor_1_out;
  wire [31:0] abs2_1_o, abs2_2_o, divu_1_o, negator_1_out;

  abs2 abs2_1 (.A(A), .O(abs2_1_o), .Sign(abs2_1_sign));
  abs2 abs2_2 (.A(B), .O(abs2_2_o), .Sign(abs2_2_sign));
  divu divu_1 (.A(abs2_1_o), .B(abs2_2_o), .O(divu_1_o));
  xor xor_1 (xor_1_out, abs2_1_sign, abs2_2_sign);
  Multiplexer #(.width(32), .enable("false")) multiplexer_1 (
    .in0(divu_1_o), .in1(negator_1_out), .out(O), .sel(xor_1_out));
  Negator #(.width(32)) negator_1 (.in(divu_1_o), .out(negator_1_out));
endmodule

module remu (
  input  [31:0] A,
  input  [31:0] B,
  output [31:0] O
);

  Divider #(.width(32)) divider_1 (.a(A), .b(B), .rem(O));  // open: out, upper
endmodule

module srl2 (
  input  [31:0] A,
  input  [31:0] B,
  output [31:0] O
);

  Shifter #(.width(32), .shift("lr")) shifter_1 (.in(A), .\dist (B[4:0]), .out(O));
endmodule

module sra2 (
  input  [31:0] A,
  input  [31:0] B,
  output [31:0] O
);

  Shifter #(.width(32), .shift("ar")) shifter_1 (.in(A), .\dist (B[4:0]), .out(O));
endmodule

module slt (
  input  [31:0] A,
  input  [31:0] B,
  output [31:0] O
);

  wire comparator_1_lt;

  Comparator #(.width(32)) comparator_1 (.a(A), .b(B), .lt(comparator_1_lt));  // open: gt, eq
  assign O = {{31{1'b0}}, comparator_1_lt};  // Bit_Extender bit_extender_1
endmodule

module sll2 (
  input  [31:0] A,
  input  [31:0] B,
  output [31:0] O
);

  Shifter #(.width(32)) shifter_1 (.in(A), .\dist (B[4:0]), .out(O));
endmodule

module cnto (
  input  [31:0] A,
  input  [31:0] B,
  output [31:0] O
);

  wire [6:0] bitadder_1_out;

  BitAdder #(.width(32)) bitadder_1 (.in0(A), .in1(B), .out(bitadder_1_out));
  assign O = {{25{1'b0}}, bitadder_1_out};  // Bit_Extender bit_extender_1
endmodule

module abs2 (
  input  [31:0] A,
  output [31:0] O,
  output Sign
);

  wire [31:0] negator_1_out;

  Multiplexer #(.width(32), .enable("false")) multiplexer_1 (.in0(A), .in1(negator_1_out), .out(O), .sel(A[31]));
  Negator #(.width(32)) negator_1 (.in(A), .out(negator_1_out));

  assign Sign = A[31];
endmodule
