// Logisim project alu.circ as structural Verilog: 18 circuits, main circuit alu
module alu (
  input  [31:0] A,
  input  [31:0] B,
  input  [3:0] ALUSel,
  output [31:0] Result
);

  wire [31:0] add3_1_o, and0_1_o, cntof_1_o, div9_1_o, divu8_1_o, mulh7_1_o, mulhu6_1_o, mult5_1_o, or1_1_o,
       remua_1_o, slle_1_o, sltd_1_o, srac_1_o, srlb_1_o, sub4_1_o, xor2_1_o;

  and0 and0_1 (.A(A), .B(B), .O(and0_1_o));
  or1 or1_1 (.A(A), .B(B), .O(or1_1_o));
  xor2 xor2_1 (.A(A), .B(B), .O(xor2_1_o));
  add3 add3_1 (.A(A), .B(B), .O(add3_1_o));
  sub4 sub4_1 (.A(A), .B(B), .O(sub4_1_o));
  mult5 mult5_1 (.A(A), .B(B), .O(mult5_1_o));
  mulhu6 mulhu6_1 (.A(A), .B(B), .O(mulhu6_1_o));
  mulh7 mulh7_1 (.A(A), .B(B), .O(mulh7_1_o));
  divu8 divu8_1 (.A(A), .B(B), .O(divu8_1_o));
  div9 div9_1 (.A(A), .B(B), .O(div9_1_o));
  remuA remua_1 (.A(A), .B(B), .O(remua_1_o));
  srlB srlb_1 (.A(A), .B(B), .O(srlb_1_o));
  sraC srac_1 (.A(A), .B(B), .O(srac_1_o));
  sltD sltd_1 (.A(A), .B(B), .O(sltd_1_o));
  sllE slle_1 (.A(A), .B(B), .O(slle_1_o));
  cntoF cntof_1 (.A(A), .B(B), .O(cntof_1_o));
  Multiplexer #(.select(4), .width(32), .enable("false")) multiplexer_1 (
    .in0(and0_1_o), .in1(or1_1_o), .in2(xor2_1_o), .in3(add3_1_o), .in4(sub4_1_o), .in5(mult5_1_o),
    .in6(mulhu6_1_o), .in7(mulh7_1_o), .in8(divu8_1_o), .in9(div9_1_o), .in10(remua_1_o), .in11(srlb_1_o),
    .in12(srac_1_o), .in13(sltd_1_o), .in14(slle_1_o), .in15(cntof_1_o), .out(Result), .sel(ALUSel));

  // Notes on the sheet:
  //   INPUTS to your circuit
  //   DON'T CHANGE THE LOCATIONS OF THE INPUTS AND OUTPUTS!
  //   OUTPUT from your circuit
endmodule

module and0 (
  input  [31:0] A,
  input  [31:0] B,
  output [31:0] O
);

  assign O = A & B;  // AND_Gate and_1, 32 bits wide
endmodule

module or1 (
  input  [31:0] A,
  input  [31:0] B,
  output [31:0] O
);

  assign O = A | B;  // OR_Gate or_1, 32 bits wide
endmodule

module xor2 (
  input  [31:0] A,
  input  [31:0] B,
  output [31:0] O
);

  assign O = A ^ B;  // XOR_Gate xor_1, 32 bits wide
endmodule

module add3 (
  input  [31:0] A,
  input  [31:0] B,
  output [31:0] O
);

  Adder #(.width(32)) adder_1 (.a(A), .b(B), .out(O));  // open: cin, cout
endmodule

module sub4 (
  input  [31:0] A,
  input  [31:0] B,
  output [31:0] O
);

  Subtractor #(.width(32)) subtractor_1 (.a(A), .b(B), .out(O));  // open: bin, bout
endmodule

module mult5 (
  input  [31:0] A,
  input  [31:0] B,
  output [31:0] O
);

  Multiplier #(.width(32)) multiplier_1 (.a(A), .b(B), .out(O));  // open: cin, cout
endmodule

module mulhu6 (
  input  [31:0] A,
  input  [31:0] B,
  output [31:0] O
);

  Multiplier #(.width(32)) multiplier_1 (.a(A), .b(B), .cout(O));  // open: out, cin
endmodule

module mulh7 (
  input  [31:0] A,
  input  [31:0] B,
  output [31:0] O
);

  wire abs2_1_sign, abs2_2_sign, adder_1_cout, xnor_1_out;
  wire [31:0] abs2_1_o, abs2_2_o, adder_2_out, bit_extender_1_out, multiplier_1_cout, multiplier_1_out,
       not_1_out, not_2_out;

  abs2 abs2_1 (.A(A), .O(abs2_1_o), .Sign(abs2_1_sign));
  abs2 abs2_2 (.A(B), .O(abs2_2_o), .Sign(abs2_2_sign));
  Multiplier #(.width(32)) multiplier_1 (
    .a(abs2_1_o), .b(abs2_2_o), .out(multiplier_1_out), .cout(multiplier_1_cout));  // open: cin
  assign not_1_out = ~multiplier_1_out;  // NOT_Gate not_1, 32 bits wide
  assign not_2_out = ~multiplier_1_cout;  // NOT_Gate not_2, 32 bits wide
  xnor xnor_1 (xnor_1_out, abs2_1_sign, abs2_2_sign);
  Adder #(.width(32)) adder_1 (.a(not_1_out), .b(32'h1), .cout(adder_1_cout));  // open: out, cin
  assign bit_extender_1_out = {{31{1'b0}}, adder_1_cout};  // Bit_Extender bit_extender_1
  Adder #(.width(32)) adder_2 (.a(bit_extender_1_out), .b(not_2_out), .out(adder_2_out));  // open: cin, cout
  Multiplexer #(.width(32), .enable("false")) multiplexer_1 (
    .in0(adder_2_out), .in1(multiplier_1_cout), .out(O), .sel(xnor_1_out));
endmodule

module divu8 (
  input  [31:0] A,
  input  [31:0] B,
  output [31:0] O
);

  Divider #(.width(32)) divider_1 (.a(A), .b(B), .out(O));  // open: upper, rem
endmodule

module div9 (
  input  [31:0] A,
  input  [31:0] B,
  output [31:0] O
);

  wire abs2_1_sign, abs2_2_sign, xor_1_out;
  wire [31:0] abs2_1_o, abs2_2_o, divu8_1_o, negator_1_out;

  abs2 abs2_1 (.A(A), .O(abs2_1_o), .Sign(abs2_1_sign));
  abs2 abs2_2 (.A(B), .O(abs2_2_o), .Sign(abs2_2_sign));
  divu8 divu8_1 (.A(abs2_1_o), .B(abs2_2_o), .O(divu8_1_o));
  xor xor_1 (xor_1_out, abs2_1_sign, abs2_2_sign);
  Multiplexer #(.width(32), .enable("false")) multiplexer_1 (
    .in0(divu8_1_o), .in1(negator_1_out), .out(O), .sel(xor_1_out));
  Negator #(.width(32)) negator_1 (.in(divu8_1_o), .out(negator_1_out));
endmodule

module remuA (
  input  [31:0] A,
  input  [31:0] B,
  output [31:0] O
);

  Divider #(.width(32)) divider_1 (.a(A), .b(B), .rem(O));  // open: out, upper
endmodule

module srlB (
  input  [31:0] A,
  input  [31:0] B,
  output [31:0] O
);

  Shifter #(.width(32), .shift("lr")) shifter_1 (.in(A), .\dist (B[4:0]), .out(O));
endmodule

module sraC (
  input  [31:0] A,
  input  [31:0] B,
  output [31:0] O
);

  Shifter #(.width(32), .shift("ar")) shifter_1 (.in(A), .\dist (B[4:0]), .out(O));
endmodule

module sltD (
  input  [31:0] A,
  input  [31:0] B,
  output [31:0] O
);

  wire comparator_1_lt;

  Comparator #(.width(32)) comparator_1 (.a(A), .b(B), .lt(comparator_1_lt));  // open: gt, eq
  assign O = {{31{1'b0}}, comparator_1_lt};  // Bit_Extender bit_extender_1
endmodule

module sllE (
  input  [31:0] A,
  input  [31:0] B,
  output [31:0] O
);

  Shifter #(.width(32)) shifter_1 (.in(A), .\dist (B[4:0]), .out(O));
endmodule

module cntoF (
  input  [31:0] A,
  input  [31:0] B,
  output [31:0] O
);

  wire [6:0] bitadder_1_out;

  BitAdder #(.width(32)) bitadder_1 (.in0(A), .in1(B), .out(bitadder_1_out));
  assign O = {{25{1'b0}}, bitadder_1_out};  // Bit_Extender bit_extender_1
endmodule

module abs2 (
  input  [31:0] A,
  output [31:0] O,
  output Sign
);

  wire [31:0] negator_1_out;

  Multiplexer #(.width(32), .enable("false")) multiplexer_1 (.in0(A), .in1(negator_1_out), .out(O), .sel(A[31]));
  Negator #(.width(32)) negator_1 (.in(A), .out(negator_1_out));

  assign Sign = A[31];
endmodule
