// Logisim project cpu.circ as structural Verilog: 15 circuits, main circuit main
module main (
  input  [31:0] INSTRUCTION,
  input  CLOCK,
  output [31:0] FETCH_ADDRESS,
  output [31:0] ra,
  output [31:0] sp,
  output [31:0] t0,
  output [31:0] t1,
  output [31:0] t2,
  output [31:0] s0,
  output [31:0] s1,
  output [31:0] a0
);

  wire BrEq, BrLT, BrUn, mem_rw, op_src, pc_sel, reg_we;
  wire [1:0] d_src, pc_src;
  wire [2:0] controller_1_imm_sel, d_sel;
  wire [3:0] alu_ctrl;
  wire [4:0] dec_1_rrd, dec_1_rrs1, dec_1_rrs2;
  wire [31:0] adder_1_out, adder_2_out, Arithmetic_Logic_Unit_result, bit_extender_1_out, bit_extender_2_out,
       bit_extender_3_out, bit_extender_4_out, DMEM_readdata, immediategenerator_1_imm, In_IF_ID_q,
       multiplexer_1_out, multiplexer_2_out, multiplexer_3_out, multiplexer_4_out, multiplexer_5_out, PC,
       PC_q, RegFile_read_data_1, rs2, WriteData;

  Adder #(.width(32)) adder_1 (.a(PC_q), .b(32'h4), .out(adder_1_out));  // open: cin, cout
  Register #(.width(32)) u_PC (.D(multiplexer_1_out), .clk(CLOCK), .Q(PC_q));  // open: en, clr
  Multiplexer #(.width(32), .enable("false")) multiplexer_1 (
    .in0(adder_1_out), .in1(Arithmetic_Logic_Unit_result), .out(multiplexer_1_out), .sel(pc_sel));
  Shifter #(.width(32), .shift("lr")) shifter_1 (.in(PC_q), .\dist (5'b00010), .out(FETCH_ADDRESS));
  Register #(.width(32)) PC_IF_ID (.D(PC_q), .clk(CLOCK), .Q(PC));  // open: en, clr
  Register #(.width(32)) In_IF_ID (.D(multiplexer_2_out), .clk(CLOCK), .Q(In_IF_ID_q));  // open: en, clr
  Multiplexer #(.width(32), .enable("false")) multiplexer_2 (
    .in0(INSTRUCTION), .in1(32'h13), .out(multiplexer_2_out), .sel(pc_sel));
  Dec dec_1 (.Instruction(In_IF_ID_q), .rrs1(dec_1_rrs1), .rrs2(dec_1_rrs2), .rrd(dec_1_rrd));
  Controller controller_1 (
    .Inst({In_IF_ID_q[30], In_IF_ID_q[25], In_IF_ID_q[14:12], In_IF_ID_q[6:2]}), .BrEq(BrEq), .BrLT(BrLT),
    .pc_sel(pc_sel), .imm_sel(controller_1_imm_sel), .BrUn(BrUn), .pc_src(pc_src), .op_src(op_src),
    .alu_ctrl(alu_ctrl), .mem_rw(mem_rw), .reg_we(reg_we), .d_src(d_src), .d_sel(d_sel));
  ImmediateGenerator immediategenerator_1 (
    .Instruction(In_IF_ID_q), .imm_sel(controller_1_imm_sel), .imm(immediategenerator_1_imm));
  regfile_main RegFile (
    .rs2(dec_1_rrs2), .rd(dec_1_rrd), .Read_Data_1(RegFile_read_data_1), .Read_Data_2(rs2), .ra(ra), .sp(sp),
    .t0(t0), .t1(t1), .t2(t2), .s0(s0), .s1(s1), .a0(a0), .rs1(dec_1_rrs1), .Write_Data(WriteData),
    .RegWEn(reg_we), .clk(CLOCK));
  BranchComparator branchcomparator_1 (.A(RegFile_read_data_1), .B(rs2), .BrUn(BrUn), .BrEq(BrEq), .BrLT(BrLT));
  Multiplexer #(.select(2), .width(32), .enable("false")) multiplexer_3 (
    .in0(RegFile_read_data_1), .in1(PC), .in2({32{1'b0}}), .out(multiplexer_3_out), .sel(pc_src));  // open: in3
  Multiplexer #(.width(32), .enable("false")) multiplexer_4 (
    .in0(rs2), .in1(immediategenerator_1_imm), .out(multiplexer_4_out), .sel(op_src));
  alu Arithmetic_Logic_Unit (
    .A(multiplexer_3_out), .B(multiplexer_4_out), .ALUSel(alu_ctrl), .Result(Arithmetic_Logic_Unit_result));
  mem_main DMEM (
    .WriteAddr(Arithmetic_Logic_Unit_result), .WriteData(rs2), .MemRW(mem_rw), .ReadData(DMEM_readdata),
    .clk(CLOCK));
  assign bit_extender_1_out = {{24{DMEM_readdata[7]}}, DMEM_readdata[7:0]};  // Bit_Extender bit_extender_1
  assign bit_extender_2_out = {{24{1'b0}}, DMEM_readdata[7:0]};  // Bit_Extender bit_extender_2
  assign bit_extender_3_out = {{16{DMEM_readdata[15]}}, DMEM_readdata[15:0]};  // Bit_Extender bit_extender_3
  assign bit_extender_4_out = {{16{1'b0}}, DMEM_readdata[15:0]};  // Bit_Extender bit_extender_4
  Multiplexer #(.select(3), .width(32), .enable("false")) multiplexer_5 (
    .in0(bit_extender_1_out), .in1(bit_extender_2_out), .in2(bit_extender_3_out), .in3(bit_extender_4_out),
    .in4(DMEM_readdata), .out(multiplexer_5_out), .sel(d_sel));  // open: in5, in6, in7
  Adder #(.width(32)) adder_2 (.a(PC), .b(32'h4), .out(adder_2_out));  // open: cin, cout
  Multiplexer #(.select(2), .width(32), .enable("false")) multiplexer_6 (
    .in0(Arithmetic_Logic_Unit_result), .in1(adder_2_out), .in2(multiplexer_5_out), .out(WriteData),
    .sel(d_src));  // open: in3

  // Other names for the same wires on the sheet: clk = CLOCK; fetch_addr[31:0] = FETCH_ADDRESS

  // Notes on the sheet:
  //   Output
  //   Inputs/Outputs from run.circ. DO NOT MOVE THESE.
  //   Inputs
  //   Inputs/Outputs from run.circ. DO NOT MOVE THESE.
endmodule

module Dec (
  input  [31:0] Instruction,
  output [4:0] rrs1,
  output [4:0] rrs2,
  output [4:0] rrd
);


  assign rrd = Instruction[11:7];
  assign rrs1 = Instruction[19:15];
  assign rrs2 = Instruction[24:20];
endmodule

module Controller (
  input  [9:0] Inst,
  input  BrEq,
  input  BrLT,
  output pc_sel,
  output [2:0] imm_sel,
  output BrUn,
  output [1:0] pc_src,
  output op_src,
  output [3:0] alu_ctrl,
  output mem_rw,
  output reg_we,
  output [1:0] d_src,
  output [2:0] d_sel
);

  wire auipc, ItypeAri, jalr, load, lui, Rtype, SBtype, Stype, UJtype;

  Comparator #(.width(5)) comparator_1 (.a(Inst[4:0]), .b({5{1'b0}}), .eq(load));  // open: gt, lt
  Comparator #(.width(5)) comparator_2 (.a(Inst[4:0]), .b(5'b00100), .eq(ItypeAri));  // open: gt, lt
  Comparator #(.width(5)) comparator_3 (.a(Inst[4:0]), .b(5'b00101), .eq(auipc));  // open: gt, lt
  Comparator #(.width(5)) comparator_4 (.a(Inst[4:0]), .b(5'b01000), .eq(Stype));  // open: gt, lt
  Comparator #(.width(5)) comparator_5 (.a(Inst[4:0]), .b(5'b01100), .eq(Rtype));  // open: gt, lt
  Comparator #(.width(5)) comparator_6 (.a(Inst[4:0]), .b(5'b01101), .eq(lui));  // open: gt, lt
  Comparator #(.width(5)) comparator_7 (.a(Inst[4:0]), .b(5'b11000), .eq(SBtype));  // open: gt, lt
  Comparator #(.width(5)) comparator_8 (.a(Inst[4:0]), .b(5'b11001), .eq(jalr));  // open: gt, lt
  Comparator #(.width(5)) comparator_9 (.a(Inst[4:0]), .b(5'b11011), .eq(UJtype));  // open: gt, lt
  PCSelect pcselect_1 (
    .jalr(jalr), .SBtype(SBtype), .UJtype(UJtype), .funct3(Inst[7:5]), .BrEq(BrEq), .BrLT(BrLT),
    .pc_sel(pc_sel));
  ImmediateSelect immediateselect_1 (
    .Stype(Stype), .SBtype(SBtype), .auipc(auipc), .lui(lui), .UJtype(UJtype), .imm_sel(imm_sel));
  BranchUnsigned branchunsigned_1 (.SBtype(SBtype), .funct3(Inst[7:5]), .BrUn(BrUn));
  PCSource pcsource_1 (.SBtype(SBtype), .UJtype(UJtype), .auipc(auipc), .lui(lui), .pc_src(pc_src));
  OperandBSource operandbsource_1 (.Rtype(Rtype), .op_src(op_src));
  ALUControl alucontrol_1 (
    .ItypeAri(ItypeAri), .Rtype(Rtype), .funct3(Inst[7:5]), .fun7(Inst[9:8]), .alu_ctrl(alu_ctrl));
  MemoryReadWrite memoryreadwrite_1 (.Stype(Stype), .mem_rw(mem_rw));
  RegisterWriteEnable registerwriteenable_1 (.Stype(Stype), .SBtype(SBtype), .reg_we(reg_we));
  DataSource datasource_1 (.jalr(jalr), .UJtype(UJtype), .load(load), .d_src(d_src));
  DataSelect dataselect_1 (.funct3(Inst[7:5]), .load(load), .d_sel(d_sel));

  // Other names for the same wires on the sheet: opc[4:0] = Inst[4:0]; funct3[2:0] = Inst[7:5]; fun7[1:0] = Inst[9:8]
endmodule

module PCSelect (
  input  jalr,
  input  SBtype,
  input  UJtype,
  input  [2:0] funct3,
  input  BrEq,
  input  BrLT,
  output pc_sel
);

  wire and_1_out, and_2_out, and_3_out, and_4_out, and_5_out, comparator_1_eq, comparator_2_eq,
       comparator_3_eq, comparator_4_eq, not_1_out, not_2_out, or_1_out;

  Comparator #(.width(2)) comparator_1 (.a({funct3[2], funct3[0]}), .b(2'b00), .eq(comparator_1_eq));  // open: gt, lt
  Comparator #(.width(2)) comparator_2 (.a({funct3[2], funct3[0]}), .b(2'b01), .eq(comparator_2_eq));  // open: gt, lt
  not not_1 (not_1_out, BrEq);
  Comparator #(.width(2)) comparator_3 (.a({funct3[2], funct3[0]}), .b(2'b10), .eq(comparator_3_eq));  // open: gt, lt
  Comparator #(.width(2)) comparator_4 (.a({funct3[2], funct3[0]}), .b(2'b11), .eq(comparator_4_eq));  // open: gt, lt
  not not_2 (not_2_out, BrLT);
  and and_1 (and_1_out, comparator_1_eq, BrEq);
  and and_2 (and_2_out, comparator_2_eq, not_1_out);
  and and_3 (and_3_out, comparator_3_eq, BrLT);
  and and_4 (and_4_out, comparator_4_eq, not_2_out);
  or or_1 (or_1_out, and_1_out, and_2_out, and_3_out, and_4_out);
  and and_5 (and_5_out, SBtype, or_1_out);
  or or_2 (pc_sel, jalr, and_5_out, UJtype);
endmodule

module ImmediateSelect (
  input  Stype,
  input  SBtype,
  input  auipc,
  input  lui,
  input  UJtype,
  output [2:0] imm_sel
);

  wire or_1_out;
  wire [2:0] and_1_out, and_2_out, and_3_out, and_4_out, bit_extender_1_out, bit_extender_2_out,
       bit_extender_3_out, bit_extender_4_out;

  or or_1 (or_1_out, auipc, lui);
  assign bit_extender_1_out = {{2{Stype}}, Stype};  // Bit_Extender bit_extender_1
  assign bit_extender_2_out = {{2{SBtype}}, SBtype};  // Bit_Extender bit_extender_2
  assign bit_extender_3_out = {{2{or_1_out}}, or_1_out};  // Bit_Extender bit_extender_3
  assign bit_extender_4_out = {{2{UJtype}}, UJtype};  // Bit_Extender bit_extender_4
  assign and_1_out = bit_extender_1_out & 3'b001;  // AND_Gate and_1, 3 bits wide
  assign and_2_out = bit_extender_2_out & 3'b010;  // AND_Gate and_2, 3 bits wide
  assign and_3_out = bit_extender_3_out & 3'b011;  // AND_Gate and_3, 3 bits wide
  assign and_4_out = bit_extender_4_out & 3'b100;  // AND_Gate and_4, 3 bits wide
  assign imm_sel = and_1_out | and_2_out | and_3_out | and_4_out;  // OR_Gate or_2, 3 bits wide
endmodule

module BranchUnsigned (
  input  SBtype,
  input  [2:0] funct3,
  output BrUn
);

  and and_1 (BrUn, SBtype, funct3[1]);
endmodule

module PCSource (
  input  SBtype,
  input  UJtype,
  input  auipc,
  input  lui,
  output [1:0] pc_src
);

  wire or_1_out;
  wire [1:0] and_1_out, and_2_out, bit_extender_1_out, bit_extender_2_out;

  assign bit_extender_1_out = {{1{or_1_out}}, or_1_out};  // Bit_Extender bit_extender_1
  or or_1 (or_1_out, SBtype, UJtype, auipc);
  assign bit_extender_2_out = {{1{lui}}, lui};  // Bit_Extender bit_extender_2
  assign and_1_out = bit_extender_1_out & 2'b01;  // AND_Gate and_1, 2 bits wide
  assign and_2_out = bit_extender_2_out & 2'b10;  // AND_Gate and_2, 2 bits wide
  assign pc_src = and_1_out | and_2_out;  // OR_Gate or_2, 2 bits wide
endmodule

module OperandBSource (
  input  Rtype,
  output op_src
);

  not not_1 (op_src, Rtype);
endmodule

module ALUControl (
  input  ItypeAri,
  input  Rtype,
  input  [2:0] funct3,
  input  [1:0] fun7,
  output [3:0] alu_ctrl
);

  wire and_7_out, and_8_out, and_9_out, and_10_out, and_11_out, and_12_out, and_13_out, and_14_out,
       and_15_out, and_16_out, and_17_out, and_18_out, comparator_1_eq, comparator_2_eq, comparator_3_eq,
       comparator_4_eq, comparator_5_eq, comparator_6_eq, comparator_7_eq, comparator_8_eq, comparator_9_eq,
       comparator_10_eq, comparator_11_eq, comparator_12_eq, comparator_13_eq, comparator_14_eq,
       comparator_15_eq, comparator_16_eq, comparator_17_eq, comparator_18_eq, comparator_19_eq,
       comparator_20_eq, comparator_21_eq, comparator_22_eq, comparator_23_eq, comparator_24_eq,
       comparator_25_eq, nor_1_out;
  wire [3:0] and_1_out, and_2_out, and_3_out, and_4_out, and_5_out, and_6_out, and_19_out, and_20_out,
       and_21_out, and_22_out, and_23_out, and_24_out, and_25_out, and_26_out, and_27_out, and_28_out,
       and_29_out, and_30_out, and_31_out, and_32_out, and_33_out, bit_extender_1_out, bit_extender_2_out,
       bit_extender_3_out, bit_extender_4_out, bit_extender_5_out, bit_extender_6_out, bit_extender_7_out,
       bit_extender_8_out, bit_extender_9_out, bit_extender_10_out, bit_extender_11_out, bit_extender_12_out,
       bit_extender_13_out, bit_extender_14_out, bit_extender_15_out, bit_extender_16_out,
       bit_extender_17_out, bit_extender_18_out, bit_extender_19_out, bit_extender_20_out,
       bit_extender_21_out, IAS, RAS;

  Comparator #(.width(3)) comparator_1 (.a(funct3), .b(3'b000), .eq(comparator_1_eq));  // open: gt, lt
  Comparator #(.width(3)) comparator_2 (.a(funct3), .b(3'b001), .eq(comparator_2_eq));  // open: gt, lt
  Comparator #(.width(3)) comparator_3 (.a(funct3), .b(3'b010), .eq(comparator_3_eq));  // open: gt, lt
  Comparator #(.width(3)) comparator_4 (.a(funct3), .b(3'b100), .eq(comparator_4_eq));  // open: gt, lt
  Comparator #(.width(3)) comparator_5 (.a(funct3), .b(3'b101), .eq(comparator_5_eq));  // open: gt, lt
  Comparator #(.width(3)) comparator_6 (.a(funct3), .b(3'b110), .eq(comparator_6_eq));  // open: gt, lt
  assign bit_extender_1_out = {{3{comparator_1_eq}}, comparator_1_eq};  // Bit_Extender bit_extender_1
  assign bit_extender_2_out = {{3{comparator_2_eq}}, comparator_2_eq};  // Bit_Extender bit_extender_2
  assign bit_extender_3_out = {{3{comparator_3_eq}}, comparator_3_eq};  // Bit_Extender bit_extender_3
  assign bit_extender_4_out = {{3{comparator_4_eq}}, comparator_4_eq};  // Bit_Extender bit_extender_4
  assign bit_extender_5_out = {{3{comparator_5_eq}}, comparator_5_eq};  // Bit_Extender bit_extender_5
  assign bit_extender_6_out = {{3{comparator_6_eq}}, comparator_6_eq};  // Bit_Extender bit_extender_6
  assign and_1_out = bit_extender_1_out & 4'b0011;  // AND_Gate and_1, 4 bits wide
  assign and_2_out = bit_extender_2_out & 4'b1110;  // AND_Gate and_2, 4 bits wide
  assign and_3_out = bit_extender_3_out & 4'b1101;  // AND_Gate and_3, 4 bits wide
  assign and_4_out = bit_extender_4_out & 4'b0010;  // AND_Gate and_4, 4 bits wide
  assign and_5_out = bit_extender_5_out & 4'b1011;  // AND_Gate and_5, 4 bits wide
  assign and_6_out = bit_extender_6_out & 4'b0001;  // AND_Gate and_6, 4 bits wide
  assign IAS = and_1_out | and_2_out | and_3_out | and_4_out | and_5_out | and_6_out;  // OR_Gate or_1, 4 bits wide
  Comparator #(.width(3)) comparator_7 (.a(funct3), .b(3'b000), .eq(comparator_7_eq));  // open: gt, lt
  Comparator #(.width(3)) comparator_8 (.a(funct3), .b(3'b001), .eq(comparator_8_eq));  // open: gt, lt
  Comparator #(.width(3)) comparator_9 (.a(funct3), .b(3'b011), .eq(comparator_9_eq));  // open: gt, lt
  Comparator #(.width(3)) comparator_10 (.a(funct3), .b(3'b100), .eq(comparator_10_eq));  // open: gt, lt
  Comparator #(.width(3)) comparator_11 (.a(funct3), .b(3'b101), .eq(comparator_11_eq));  // open: gt, lt
  Comparator #(.width(3)) comparator_12 (.a(funct3), .b(3'b110), .eq(comparator_12_eq));  // open: gt, lt
  Comparator #(.width(3)) comparator_13 (.a(funct3), .b(3'b111), .eq(comparator_13_eq));  // open: gt, lt
  Comparator #(.width(2)) comparator_14 (.a(fun7), .b(2'b00), .eq(comparator_14_eq));  // open: gt, lt
  Comparator #(.width(2)) comparator_15 (.a(fun7), .b(2'b01), .eq(comparator_15_eq));  // open: gt, lt
  Comparator #(.width(2)) comparator_16 (.a(fun7), .b(2'b10), .eq(comparator_16_eq));  // open: gt, lt
  Comparator #(.width(2)) comparator_17 (.a(fun7), .b(2'b00), .eq(comparator_17_eq));  // open: gt, lt
  Comparator #(.width(2)) comparator_18 (.a(fun7), .b(2'b01), .eq(comparator_18_eq));  // open: gt, lt
  Comparator #(.width(2)) comparator_19 (.a(fun7), .b(2'b01), .eq(comparator_19_eq));  // open: gt, lt
  Comparator #(.width(2)) comparator_20 (.a(fun7), .b(2'b00), .eq(comparator_20_eq));  // open: gt, lt
  Comparator #(.width(2)) comparator_21 (.a(fun7), .b(2'b01), .eq(comparator_21_eq));  // open: gt, lt
  Comparator #(.width(2)) comparator_22 (.a(fun7), .b(2'b00), .eq(comparator_22_eq));  // open: gt, lt
  Comparator #(.width(2)) comparator_23 (.a(fun7), .b(2'b01), .eq(comparator_23_eq));  // open: gt, lt
  Comparator #(.width(2)) comparator_24 (.a(fun7), .b(2'b00), .eq(comparator_24_eq));  // open: gt, lt
  Comparator #(.width(2)) comparator_25 (.a(fun7), .b(2'b01), .eq(comparator_25_eq));  // open: gt, lt
  and and_7 (and_7_out, comparator_14_eq, comparator_7_eq);
  and and_8 (and_8_out, comparator_15_eq, comparator_7_eq);
  and and_9 (and_9_out, comparator_16_eq, comparator_7_eq);
  and and_10 (and_10_out, comparator_17_eq, comparator_8_eq);
  and and_11 (and_11_out, comparator_18_eq, comparator_8_eq);
  and and_12 (and_12_out, comparator_19_eq, comparator_9_eq);
  and and_13 (and_13_out, comparator_20_eq, comparator_10_eq);
  and and_14 (and_14_out, comparator_21_eq, comparator_10_eq);
  and and_15 (and_15_out, comparator_22_eq, comparator_11_eq);
  and and_16 (and_16_out, comparator_23_eq, comparator_11_eq);
  and and_17 (and_17_out, comparator_24_eq, comparator_12_eq);
  and and_18 (and_18_out, comparator_25_eq, comparator_13_eq);
  assign bit_extender_7_out = {{3{and_7_out}}, and_7_out};  // Bit_Extender bit_extender_7
  assign and_19_out = bit_extender_7_out & 4'b0011;  // AND_Gate and_19, 4 bits wide
  assign bit_extender_8_out = {{3{and_8_out}}, and_8_out};  // Bit_Extender bit_extender_8
  assign and_20_out = bit_extender_8_out & 4'b0101;  // AND_Gate and_20, 4 bits wide
  assign bit_extender_9_out = {{3{and_9_out}}, and_9_out};  // Bit_Extender bit_extender_9
  assign and_21_out = bit_extender_9_out & 4'b0100;  // AND_Gate and_21, 4 bits wide
  assign bit_extender_10_out = {{3{and_10_out}}, and_10_out};  // Bit_Extender bit_extender_10
  assign and_22_out = bit_extender_10_out & 4'b1110;  // AND_Gate and_22, 4 bits wide
  assign bit_extender_11_out = {{3{and_11_out}}, and_11_out};  // Bit_Extender bit_extender_11
  assign and_23_out = bit_extender_11_out & 4'b0111;  // AND_Gate and_23, 4 bits wide
  assign bit_extender_12_out = {{3{and_12_out}}, and_12_out};  // Bit_Extender bit_extender_12
  assign and_24_out = bit_extender_12_out & 4'b0110;  // AND_Gate and_24, 4 bits wide
  assign bit_extender_13_out = {{3{and_13_out}}, and_13_out};  // Bit_Extender bit_extender_13
  assign and_25_out = bit_extender_13_out & 4'b0010;  // AND_Gate and_25, 4 bits wide
  assign bit_extender_14_out = {{3{and_14_out}}, and_14_out};  // Bit_Extender bit_extender_14
  assign and_26_out = bit_extender_14_out & 4'b1001;  // AND_Gate and_26, 4 bits wide
  assign bit_extender_15_out = {{3{and_15_out}}, and_15_out};  // Bit_Extender bit_extender_15
  assign and_27_out = bit_extender_15_out & 4'b1011;  // AND_Gate and_27, 4 bits wide
  assign bit_extender_16_out = {{3{and_16_out}}, and_16_out};  // Bit_Extender bit_extender_16
  assign and_28_out = bit_extender_16_out & 4'b1000;  // AND_Gate and_28, 4 bits wide
  assign bit_extender_17_out = {{3{and_17_out}}, and_17_out};  // Bit_Extender bit_extender_17
  assign and_29_out = bit_extender_17_out & 4'b0001;  // AND_Gate and_29, 4 bits wide
  assign bit_extender_18_out = {{3{and_18_out}}, and_18_out};  // Bit_Extender bit_extender_18
  assign and_30_out = bit_extender_18_out & 4'b1010;  // AND_Gate and_30, 4 bits wide
  assign RAS = and_19_out | and_20_out | and_21_out | and_22_out | and_23_out | and_24_out | and_25_out | and_26_out | and_27_out | and_28_out | and_29_out | and_30_out;  // OR_Gate or_2, 4 bits wide
  nor nor_1 (nor_1_out, Rtype, ItypeAri);
  assign bit_extender_19_out = {{3{Rtype}}, Rtype};  // Bit_Extender bit_extender_19
  assign bit_extender_20_out = {{3{ItypeAri}}, ItypeAri};  // Bit_Extender bit_extender_20
  assign bit_extender_21_out = {{3{nor_1_out}}, nor_1_out};  // Bit_Extender bit_extender_21
  assign and_31_out = bit_extender_19_out & RAS;  // AND_Gate and_31, 4 bits wide
  assign and_32_out = bit_extender_20_out & IAS;  // AND_Gate and_32, 4 bits wide
  assign and_33_out = bit_extender_21_out & 4'b0011;  // AND_Gate and_33, 4 bits wide
  assign alu_ctrl = and_31_out | and_32_out | and_33_out;  // OR_Gate or_3, 4 bits wide
endmodule

module MemoryReadWrite (
  input  Stype,
  output mem_rw
);


  assign mem_rw = Stype;
endmodule

module RegisterWriteEnable (
  input  Stype,
  input  SBtype,
  output reg_we
);

  nor nor_1 (reg_we, Stype, SBtype);
endmodule

module DataSource (
  input  jalr,
  input  UJtype,
  input  load,
  output [1:0] d_src
);

  wire or_1_out;
  wire [1:0] and_1_out, and_2_out, bit_extender_1_out, bit_extender_2_out;

  assign bit_extender_1_out = {{1{or_1_out}}, or_1_out};  // Bit_Extender bit_extender_1
  or or_1 (or_1_out, jalr, UJtype);
  assign bit_extender_2_out = {{1{load}}, load};  // Bit_Extender bit_extender_2
  assign and_1_out = bit_extender_1_out & 2'b01;  // AND_Gate and_1, 2 bits wide
  assign and_2_out = bit_extender_2_out & 2'b10;  // AND_Gate and_2, 2 bits wide
  assign d_src = and_1_out | and_2_out;  // OR_Gate or_2, 2 bits wide
endmodule

module DataSelect (
  input  [2:0] funct3,
  input  load,
  output [2:0] d_sel
);

  wire comparator_1_eq, comparator_2_eq, comparator_3_eq, comparator_4_eq;
  wire [2:0] and_1_out, and_2_out, and_3_out, and_4_out, bit_extender_1_out, bit_extender_2_out,
       bit_extender_3_out, bit_extender_4_out, or_1_out;

  Comparator #(.width(3)) comparator_1 (.a(funct3), .b(3'b100), .eq(comparator_1_eq));  // open: gt, lt
  assign bit_extender_1_out = {{2{comparator_1_eq}}, comparator_1_eq};  // Bit_Extender bit_extender_1
  Comparator #(.width(3)) comparator_2 (.a(funct3), .b(3'b001), .eq(comparator_2_eq));  // open: gt, lt
  assign bit_extender_2_out = {{2{comparator_2_eq}}, comparator_2_eq};  // Bit_Extender bit_extender_2
  assign bit_extender_3_out = {{2{comparator_3_eq}}, comparator_3_eq};  // Bit_Extender bit_extender_3
  Comparator #(.width(3)) comparator_3 (.a(funct3), .b(3'b101), .eq(comparator_3_eq));  // open: gt, lt
  Comparator #(.width(3)) comparator_4 (.a(funct3), .b(3'b010), .eq(comparator_4_eq));  // open: gt, lt
  assign bit_extender_4_out = {{2{comparator_4_eq}}, comparator_4_eq};  // Bit_Extender bit_extender_4
  assign and_1_out = bit_extender_1_out & 3'b001;  // AND_Gate and_1, 3 bits wide
  assign and_2_out = bit_extender_2_out & 3'b010;  // AND_Gate and_2, 3 bits wide
  assign and_3_out = bit_extender_3_out & 3'b011;  // AND_Gate and_3, 3 bits wide
  assign and_4_out = bit_extender_4_out & 3'b100;  // AND_Gate and_4, 3 bits wide
  assign or_1_out = and_1_out | and_2_out | and_3_out | and_4_out;  // OR_Gate or_1, 3 bits wide
  Multiplexer #(.width(3), .enable("false")) multiplexer_1 (.in0(3'b100), .in1(or_1_out), .out(d_sel), .sel(load));
endmodule

module ImmediateGenerator (
  input  [31:0] Instruction,
  input  [2:0] imm_sel,
  output [31:0] imm
);

  wire [31:0] bit_extender_1_out, bit_extender_2_out, bit_extender_3_out, bit_extender_4_out;

  assign bit_extender_1_out = {{20{Instruction[31]}}, Instruction[31:20]};  // Bit_Extender bit_extender_1
  assign bit_extender_2_out = {{20{Instruction[31]}}, {Instruction[31:25], Instruction[11:7]}};  // Bit_Extender bit_extender_2
  assign bit_extender_3_out = {{19{Instruction[31]}}, {Instruction[31], Instruction[7], Instruction[30:25], Instruction[11:8], 1'b0}};  // Bit_Extender bit_extender_3
  assign bit_extender_4_out = {{11{Instruction[31]}}, {Instruction[31], Instruction[19:12], Instruction[20], Instruction[30:21], 1'b0}};  // Bit_Extender bit_extender_4
  Multiplexer #(.select(3), .width(32), .enable("false")) multiplexer_1 (
    .in0(bit_extender_1_out), .in1(bit_extender_2_out), .in2(bit_extender_3_out),
    .in3({Instruction[31:12], {12{1'b0}}}), .in4(bit_extender_4_out), .out(imm), .sel(imm_sel));  // open: in5, in6, in7
endmodule

module BranchComparator (
  input  [31:0] A,
  input  [31:0] B,
  input  BrUn,
  output BrEq,
  output BrLT
);

  wire comparator_2_lt, comparator_3_lt;

  Comparator #(.width(32)) comparator_1 (.a(A), .b(B), .eq(BrEq));  // open: gt, lt
  Comparator #(.width(32)) comparator_2 (.a(A), .b(B), .lt(comparator_2_lt));  // open: gt, eq
  Comparator #(.width(32), .mode("unsigned")) comparator_3 (.a(A), .b(B), .lt(comparator_3_lt));  // open: gt, eq
  Multiplexer #(.enable("false")) multiplexer_1 (.in0(comparator_2_lt), .in1(comparator_3_lt), .out(BrLT), .sel(BrUn));
endmodule
