// Logisim project mem.circ as structural Verilog: 1 circuit, main circuit main
module main (
  input  [31:0] WriteAddr,
  input  [31:0] WriteData,
  input  MemRW,
  input  clk,
  output [31:0] ReadData
);

  RAM #(.addrWidth(24), .dataWidth(32), .trigger("falling"), .databus("bibus")) ram_1 ();  // open: addr, we, oe, clk, din, dout

  // Notes on the sheet:
  //   INPUTS to your circuit
  //   OUTPUT from your circuit
endmodule
